# Fritzing sketch câblage (saved by Fritzing 0.9.8b)
breadboards: 1

parts:
  Composant1 = Arduino BT
  DFRobot_DFPlayer_Mini1 = DFRobot DFPlayer Mini [part_number=DFR0299]
  J1 = Basic Force Sensing Resistor (FSR) [package=THT]
  R1 = Resistor [tolerance=±5% power=0.25 resistance=10k package=THT]
  SPKR1 = Loudspeaker
  R2 = Resistor [tolerance=±5% resistance=1k package="0805 [SMD]"]

nets:
  N1: Composant1.SS/PWM_D10, DFRobot_DFPlayer_Mini1.TX, DFRobot_DFPlayer_Mini1.DAC_R
  N2: Composant1.MOSI/PWM_D11, R2.Pin_0
  N3: Composant1.GND, DFRobot_DFPlayer_Mini1.GND-1, DFRobot_DFPlayer_Mini1.GND-2, R1.Pin_0
  N4: Composant1.A0, J1.pin_0, R1.Pin_1
  5V: Composant1.5V, DFRobot_DFPlayer_Mini1.VCC, DFRobot_DFPlayer_Mini1.RX, J1.pin_1, R2.Pin_1
  N5: DFRobot_DFPlayer_Mini1.SPK_1, SPKR1.pin1
  N6: DFRobot_DFPlayer_Mini1.SPK_2, SPKR1.pin2
